# Fritzing sketch circuit_diagram (saved by Fritzing 0.9.3b)
breadboards: 3

parts:
  Arduino_Nano = Arduino Nano (Rev3.0)
  Raspberry_Pi_3B+ = Raspberry Pi 3 [part_number=RPI-3-V1.2]
  IC1 = L293D [package=THT]
  TILT_SERVO = Basic Servo
  STEERING_SERVO = Basic Servo
  PAN_SERVO = Basic Servo
  VCC1 = Battery
  M1 = DC Motor
  VCC2 = Battery
  VCC3 = Battery

nets:
  GND: Arduino_Nano.GND, Raspberry_Pi_3B+.GND, IC1.0V, TILT_SERVO.gnd, STEERING_SERVO.gnd, PAN_SERVO.gnd, VCC3.-
  N1: Arduino_Nano.D4, STEERING_SERVO.pulse
  N2: Arduino_Nano.D5, PAN_SERVO.pulse
  N3: Arduino_Nano.D6, TILT_SERVO.pulse
  N4: Raspberry_Pi_3B+.GIPO25, IC1.In_2
  N5: Raspberry_Pi_3B+.GIPO24, IC1.In_1
  N6: Raspberry_Pi_3B+.GIPO23, IC1.Enable_1
  VCC: Raspberry_Pi_3B+.5V, IC1.+V, TILT_SERVO.vcc, PAN_SERVO.vcc
  N7: IC1.Out_1_(_Controlled_by_Enable_1_), M1.pin_1
  N8: IC1.Out_2_(_Controlled_by_Enable_1_), M1.pin_2
  N9: IC1.+Vmotor, STEERING_SERVO.vcc, VCC1.+
  N10: VCC1.-, VCC2.+
  N11: VCC2.-, VCC3.+
